// Logisim project control.circ as structural Verilog: 3 circuits, main circuit control
module control (
  input  lsb,
  input  start,
  input  in_3,
  output [1:0] out_4,
  output [1:0] out_5
);

  wire and_1_out, and_2_out, and_3_out, and_4_out, and_5_out, and_6_out, and_7_out, check_end_1_end,
       not_1_out, not_2_out, not_3_out, not_4_out, not_5_out, not_6_out, not_7_out, not_8_out, not_9_out,
       not_10_out, or_1_out, or_2_out, or_3_out, register_1_q, register_2_q, register_3_q;

  not not_1 (not_1_out, register_3_q);
  not not_2 (not_2_out, start);
  not not_3 (not_3_out, start);
  not not_4 (not_4_out, check_end_1_end);
  not not_5 (not_5_out, register_1_q);
  not not_6 (not_6_out, register_3_q);
  not not_7 (not_7_out, register_1_q);
  not not_8 (not_8_out, register_2_q);
  not not_9 (not_9_out, register_3_q);
  not not_10 (not_10_out, register_2_q);
  and and_1 (and_1_out, check_end_1_end, start, register_2_q, not_1_out);
  and and_2 (and_2_out, not_2_out, register_2_q);
  and and_3 (and_3_out, start, register_3_q);
  and and_4 (and_4_out, not_3_out, register_3_q);
  and and_5 (and_5_out, not_4_out, start, not_5_out, not_6_out);
  and and_6 (and_6_out, start, not_7_out, not_8_out, not_9_out);
  and and_7 (and_7_out, lsb, not_10_out, register_3_q);
  or or_1 (or_1_out, register_1_q, and_1_out);
  or or_2 (or_2_out, and_2_out, and_3_out);
  or or_3 (or_3_out, and_4_out, and_5_out, and_6_out, and_7_out);
  Register #(.width(1)) register_1 (.D(or_1_out), .Q(register_1_q), .clk(in_3));  // open: en, clr
  Register #(.width(1)) register_2 (.D(or_2_out), .Q(register_2_q), .clk(in_3));  // open: en, clr
  Register #(.width(1)) register_3 (.D(or_3_out), .Q(register_3_q), .clk(in_3));  // open: en, clr
  mul mul_1 (.s0(register_1_q), .s1(register_2_q), .s2(register_3_q), .out_4(out_4), .out_5(out_5));
  check_end check_end_1 (
    .s0(register_1_q), .s1(register_2_q), .s2(register_3_q), .clock(in_3), .\end (check_end_1_end));
endmodule

module check_end (
  input  s0,
  input  s1,
  input  s2,
  input  clock,
  output \end 
);

  wire and_1_out, comparator_1_eq, comparator_2_eq, comparator_3_eq;

  Comparator #(.width(1)) comparator_1 (.a(1'b0), .b(s0), .eq(comparator_1_eq));  // open: gt, lt
  and and_1 (and_1_out, comparator_1_eq, comparator_2_eq, comparator_3_eq);
  Comparator #(.width(1)) comparator_2 (.a(s1), .b(1'b1), .eq(comparator_2_eq));  // open: gt, lt
  Comparator #(.width(1)) comparator_3 (.a(s2), .b(1'b0), .eq(comparator_3_eq));  // open: gt, lt
  Counter #(.width(5), .max('h1f)) counter_1 (.count(and_1_out), .carry(\end ), .clk(clock));  // open: load, D, Q, clr
endmodule

module mul (
  input  s0,
  input  s1,
  input  s2,
  output [1:0] out_4,
  output [1:0] out_5
);

  wire and_1_out, and_2_out, not_1_out, not_2_out;

  and and_1 (and_1_out, s1, not_1_out);
  not not_1 (not_1_out, s2);
  and and_2 (and_2_out, s0, s2);
  and and_3 (out_4[0], s1, s2);
  or or_1 (out_5[1], s2, s0);
  and and_4 (out_5[0], s1, not_2_out);
  not not_2 (not_2_out, s2);
  or or_2 (out_4[1], and_1_out, and_2_out);
endmodule
