// Logisim project datapath.circ as structural Verilog: 3 circuits, main circuit datapath
module datapath (
  input  [31:0] in_1,
  input  [31:0] in_2,
  input  [1:0] m0,
  input  [1:0] p0,
  input  in_5,
  output [31:0] firts32_bit,
  output [31:0] last32_bit,
  output lsb
);

  wire adder_1_cout, register_4_q;
  wire [31:0] adder_1_out, multiplexer_1_out, multiplexer_2_out, register_1_q, shifter_64_bit_1_out_4,
       shifter_64_bit_1_out_5;

  Multiplexer #(.select(2), .width(32)) multiplexer_1 (
    .in0(firts32_bit), .in1(adder_1_out), .in2(shifter_64_bit_1_out_4), .out(multiplexer_1_out), .sel(p0));  // open: in3, en
  Register #(.width(32)) register_1 (.D(in_2), .Q(register_1_q), .clk(in_5));  // open: en, clr
  Register #(.width(32)) register_2 (.D(multiplexer_1_out), .Q(firts32_bit), .clk(in_5));  // open: en, clr
  Register #(.width(32)) register_3 (.D(multiplexer_2_out), .Q(last32_bit), .clk(in_5));  // open: en, clr
  Multiplexer #(.select(2), .width(32)) multiplexer_2 (
    .in0(in_1), .in1(shifter_64_bit_1_out_5), .in2(last32_bit), .out(multiplexer_2_out), .sel(m0));  // open: in3, en
  Register #(.width(1)) register_4 (.D(adder_1_cout), .Q(register_4_q), .clk(in_5));  // open: en, clr
  Adder #(.width(32)) adder_1 (.a(register_1_q), .b(firts32_bit), .out(adder_1_out), .cout(adder_1_cout));  // open: cin
  shifter_64_bit shifter_64_bit_1 (
    .in_1(firts32_bit), .in_2(last32_bit), .in_3(register_4_q), .out_4(shifter_64_bit_1_out_4),
    .out_5(shifter_64_bit_1_out_5));
  get_lsb get_lsb_1 (.in_1(last32_bit), .out_2(lsb));
endmodule

module get_lsb (
  input  [31:0] in_1,
  output out_2
);


  assign out_2 = in_1[0];
endmodule

module shifter_64_bit (
  input  [31:0] in_1,
  input  [31:0] in_2,
  input  in_3,
  output [31:0] out_4,
  output [31:0] out_5
);


  assign out_4 = {in_3, in_1[31:1]};
  assign out_5 = {in_1[0], in_2[31:1]};
endmodule
