// Logisim project mult32.circ as structural Verilog: 1 circuit, main circuit mult32
module mult32 (
  input  in_1,
  output [31:0] out_2,
  output [31:0] out_3
);

  wire clock_1_out, datapath_1_lsb;
  wire [1:0] control_1_out_4, control_1_out_5;

  Clock clock_1 (.out(clock_1_out));
  control control_1 (
    .lsb(datapath_1_lsb), .start(in_1), .in_3(clock_1_out), .out_4(control_1_out_4), .out_5(control_1_out_5));
  datapath datapath_1 (
    .in_1(32'h3), .in_2(32'h8), .in_5(clock_1_out), .firts32_bit(out_2), .last32_bit(out_3),
    .lsb(datapath_1_lsb), .m0(control_1_out_5), .p0(control_1_out_4));
endmodule
